// Logisim project PentaCortexA2.circ as structural Verilog: 7 circuits, main circuit main
module PentaCortexA2Core (
  input  nCLK,
  input  RST,
  input  MISO,
  input  [31:0] BUSDATAA,
  input  [31:0] BUSDATAB,
  input  PB0,
  input  PB1,
  input  PB2,
  input  PB3,
  input  PB4,
  input  PB5,
  input  PB6,
  input  PB7,
  input  PB8,
  input  PB9,
  input  PB10,
  input  PB11,
  input  PB12,
  input  PB13,
  input  PB14,
  input  PB15,
  input  PB16,
  input  PB17,
  input  PB18,
  input  PB19,
  input  PB20,
  input  PB21,
  input  PB22,
  input  PB23,
  input  PB24,
  input  PB25,
  input  PB26,
  input  PB27,
  input  PB28,
  input  PB29,
  input  PB30,
  input  PB31,
  input  [31:0] ROMData,
  input  [31:0] RAM0R,
  input  [31:0] RAM1R,
  output BUSRST,
  output BUSCLK,
  output MOSI,
  output SCK,
  output [7:0] BUSADDRA,
  output [7:0] BUSADDRB,
  output [7:0] BUSADDRC,
  output [31:0] BUSDATAC,
  output PB0_2,
  output PB1_2,
  output PB2_2,
  output PB3_2,
  output PB4_2,
  output PB5_2,
  output PB6_2,
  output PB7_2,
  output PB8_2,
  output PB9_2,
  output PB10_2,
  output PB11_2,
  output PB12_2,
  output PB13_2,
  output PB14_2,
  output PB15_2,
  output [14:0] ROMAddr,
  output PB16_2,
  output PB17_2,
  output PB18_2,
  output PB19_2,
  output PB20_2,
  output PB21_2,
  output [13:0] RAM0Addr,
  output PB22_2,
  output PB23_2,
  output PB24_2,
  output PB25_2,
  output PB26_2,
  output PB27_2,
  output [13:0] RAM1Addr,
  output PB28_2,
  output PB29_2,
  output PB30_2,
  output PB31_2,
  output RAM0RF,
  output RAM0WF,
  output [31:0] RAM0W,
  output RAM1RF,
  output RAM1WF,
  output [31:0] RAM1W
);

  wire adder_1_cout, adder_4_cout, ADDF, ADDI, ALUZero, AND, and_2_out, and_3_out, and_5_out, and_6_out,
       and_7_out, and_8_out, and_9_out, and_10_out, and_12_out, and_13_out, and_14_out, and_15_out,
       and_16_out, and_17_out, and_18_out, and_19_out, and_20_out, and_21_out, and_22_out, and_23_out,
       and_31_out, and_32_out, BOR, calculator_1_p1, CCC, comparator_1_eq, comparator_2_eq, comparator_3_eq,
       comparator_4_lt, comparator_5_lt, comparator_6_eq, comparator_7_eq, COS, counter_2_carry,
       counter_3_carry, decoder_1_out0, decoder_1_out1, decoder_1_out2, decoder_1_out3, decoder_1_out4,
       decoder_1_out5, decoder_1_out6, decoder_1_out7, decoder_2_out0, decoder_2_out1, decoder_2_out2,
       decoder_2_out3, decoder_2_out4, decoder_2_out5, decoder_2_out6, decoder_2_out7, DIVF, DIVI, DNI, DR,
       End_Of_Flash, FTI, FTU, I1, I2, I3, IFC, IFR, INV, IS1, IS2, IS3, ITF, JMC, JMR, LOD, MDRF, MDWF,
       MINF, MINI, MOD, MULF, MULI, n1wordregs_26_inputaddrmatch, NOCLK, NOCLKF, not_1_out, not_2_out,
       not_3_out, not_4_out, not_5_out, not_6_out, not_7_out, not_8_out, not_9_out, not_10_out, not_11_out,
       not_12_out, not_13_out, not_14_out, not_15_out, not_16_out, not_18_out, not_19_out, or_1_out,
       or_2_out, or_3_out, or_4_out, or_5_out, or_6_out, or_7_out, or_8_out, or_9_out, or_10_out, or_11_out,
       or_13_out, or_14_out, or_15_out, or_18_out, or_20_out, or_21_out, or_25_out, or_27_out,
       pull_resistor_22_node, RAMRF, RAMWF, RSTFlag, s_r_ff_1_q, s_r_ff_6_q, shift_register_1_q0,
       shift_register_3_out, shift_register_3_q2, shift_register_4_q0, shift_register_4_q1,
       shift_register_5_q2, shift_register_5_q3, shift_register_6_q1, shift_register_8_out,
       shift_register_8_q0, SI, SIN, SPIMWF, SPIRWF, SPMWF, SPSP_minus, SPSP_plus, SQR, SREGWF,
       Stack_Overflow, Stack_Underflow, STI, STR, subtractor_1_bout, SUC, SUR, TI, UTF, WRC, WURR;
  wire [2:0] adder_1_out, counter_3_q;
  wire [5:0] demultiplexer_2_out1, demultiplexer_2_out2, demultiplexer_2_out3, demultiplexer_2_out4,
       demultiplexer_2_out5, demultiplexer_2_out6, demultiplexer_2_out7;
  wire [15:0] adder_2_out, bit_extender_17_out, bit_extender_18_out, bit_extender_19_out,
       controlled_buffer_54_out, MDA, MPA, multiplexer_3_out, multiplier_1_cout, multiplier_1_cout_2, SP1O,
       SP2O, SP3O, SP4O, SP5O, SP6O, SP7O, SP8O, SPIMWD, SPMWD, undriven;
  wire [16:0] SP1I, SP2I, SP3I, SP4I, SP5I, SP6I, SP7I, SP8I;
  wire [31:0] adder_3_out, adder_4_out, ALU, and_29_out, bit_extender_1_out, bit_extender_2_out,
       bit_extender_5_out, bit_extender_6_out, bit_extender_9_out, bit_extender_10_out, bit_extender_13_out,
       bit_extender_14_out, calculator_1_p2, calculator_1_p3, calculator_1_p4, calculator_1_p5, CCCD,
       cos_1_p1, divider_1_out, divider_1_rem, INTB, intto32bitfp_1_p2, MDRD, MPD, multiplexer_1_out,
       multiplexer_2_out, multiplexer_4_out, multiplexer_5_out, multiplexer_7_out, multiplexer_8_out,
       multiplexer_9_out, multiplexer_11_out, multiplexer_12_out, multiplexer_13_out, multiplexer_14_out,
       multiplexer_15_out, multiplexer_19_out, multiplexer_20_out, multiplier_1_out, n1wordregs_1_data,
       n1wordregs_2_data, n1wordregs_3_data, n1wordregs_4_data, n1wordregs_6_data, n1wordregs_7_data,
       n1wordregs_8_data, n1wordregs_9_data, n1wordregs_10_data, n1wordregs_11_data, n1wordregs_12_data,
       n1wordregs_13_data, n1wordregs_15_data, n1wordregs_16_data, n1wordregs_17_data, n1wordregs_18_data,
       n1wordregs_19_data, n1wordregs_20_data, n1wordregs_21_data, n1wordregs_22_data, n1wordregs_23_data,
       n1wordregs_24_data, n1wordregs_26_data, n1wordregs_27_data, n1wordregs_28_data, n1wordregs_29_data,
       n1wordregs_30_data, n1wordregs_31_data, n32bitfptoint_1_p2, n32bitfptouint_1_p2, not_17_out,
       or_12_out, or_22_out, or_23_out, or_24_out, or_26_out, or_28_out, RDA, RDB, sin_1_p1, SPIRR, SPIRW,
       sqrt_1_p1, SREGR, SREGW, subtractor_1_out, uintto32bitfp_1_p2;

  Pull_Resistor pull_resistor_1 (.node(SPSP_plus));
  Pull_Resistor pull_resistor_2 (.node(SPSP_minus));
  Pull_Resistor pull_resistor_3 (.node(SI));
  Pull_Resistor pull_resistor_4 (.node(NOCLKF));
  Pull_Resistor pull_resistor_5 (.node(BUSRST));
  Pull_Resistor pull_resistor_6 (.node(Stack_Overflow));
  Pull_Resistor pull_resistor_7 (.node(ALUZero));
  Pull_Resistor pull_resistor_8 (.node(DNI));
  Pull_Resistor pull_resistor_9 (.node(WURR));
  Shift_Register #(.length(1)) shift_register_1 (
    .shift(1'b1), .in(SPIRR[23]), .clk(nCLK), .load(1'b0), .clr(BUSRST), .q0(shift_register_1_q0));  // open: out, d0
  Shift_Register shift_register_2 (
    .shift(shift_register_1_q0), .in(MISO), .out(MOSI), .load(SPIRR[23]), .clr(BUSRST), .d0(SPIRR[31]),
    .q0(SPIRW[31]), .d1(SPIRR[30]), .q1(SPIRW[30]), .d2(SPIRR[29]), .q2(SPIRW[29]), .d3(SPIRR[28]),
    .q3(SPIRW[28]), .d4(SPIRR[27]), .q4(SPIRW[27]), .d5(SPIRR[26]), .q5(SPIRW[26]), .d6(SPIRR[25]),
    .q6(SPIRW[25]), .d7(SPIRR[24]), .q7(SPIRW[24]));  // open: clk
  Pull_Resistor pull_resistor_10 (.node(RAMWF));
  Pull_Resistor pull_resistor_11 (.node(RAMRF));
  Pull_Resistor pull_resistor_12 (.node(SPMWF));
  Pull_Resistor pull_resistor_13 (.node(SREGWF));
  Pull_Resistor pull_resistor_14 (.node(SPIMWF));
  Pull_Resistor pull_resistor_15 (.node(RSTFlag));
  assign RDA = comparator_1_eq ? {32{1'b0}} : 32'bz;  // Controlled_Buffer controlled_buffer_1
  Comparator comparator_1 (.a(BUSADDRA), .b({8{1'b0}}), .eq(comparator_1_eq));  // open: gt, lt
  assign RDB = comparator_2_eq ? {32{1'b0}} : 32'bz;  // Controlled_Buffer controlled_buffer_2
  Comparator comparator_2 (.a(BUSADDRB), .b({8{1'b0}}), .eq(comparator_2_eq));  // open: gt, lt
  and and_1 (SI, SPIRR[22], SPIRWF);
  S_R_Flip_Flop s_r_ff_1 (
    .S(SPIRR[23]), .clk(nCLK), .R(SPIRWF), .Q(s_r_ff_1_q), .preset(1'b0), .reset(BUSRST), .en(1'b1));  // open: Qn
  S_R_Flip_Flop #(.trigger("low")) s_r_ff_2 (
    .S(IS1), .clk(nCLK), .R(1'b0), .Q(I1), .preset(1'b0), .reset(or_1_out), .en(not_1_out));  // open: Qn
  Pull_Resistor pull_resistor_16 (.node(IS1));
  S_R_Flip_Flop #(.trigger("low")) s_r_ff_3 (
    .S(IS2), .clk(nCLK), .R(1'b0), .Q(I2), .preset(1'b0), .reset(or_1_out), .en(not_1_out));  // open: Qn
  Pull_Resistor pull_resistor_17 (.node(IS2));
  Pull_Resistor pull_resistor_18 (.node(IS3));
  S_R_Flip_Flop #(.trigger("low")) s_r_ff_4 (
    .S(IS3), .clk(nCLK), .R(1'b0), .Q(I3), .preset(1'b0), .reset(or_1_out), .en(not_1_out));  // open: Qn
  or or_1 (or_1_out, shift_register_3_out, BUSRST);
  not not_1 (not_1_out, pull_resistor_22_node);
  assign bit_extender_1_out = {{16{1'b0}}, SP1I[16:1]};  // Bit_Extender bit_extender_1
  Multiplexer #(.width(32), .disabled(0), .enable("false")) multiplexer_1 (
    .in0(bit_extender_1_out), .in1(BUSDATAC), .out(multiplexer_1_out), .sel(not_2_out));
  not not_2 (not_2_out, SP1I[0]);
  assign bit_extender_2_out = {{16{1'b0}}, SP5I[16:1]};  // Bit_Extender bit_extender_2
  Multiplexer #(.width(32), .disabled(0), .enable("false")) multiplexer_2 (
    .in0(bit_extender_2_out), .in1(BUSDATAC), .out(multiplexer_2_out), .sel(not_3_out));
  not not_3 (not_3_out, SP5I[0]);
  or or_2 (or_2_out, Stack_Underflow, Stack_Overflow, End_Of_Flash, RSTFlag, RST);
  Counter #(.width(3), .max('h7)) counter_1 (
    .load(1'b0), .count(1'b1), .carry(SPIRWF), .clk(and_2_out), .clr(BUSRST));  // open: D, Q
  and and_2 (and_2_out, nCLK, s_r_ff_1_q);
  nand nand_1 (SCK, SPIRWF, nCLK);
  Pull_Resistor pull_resistor_19 (.node(SP1I[0]));
  // Probe on n1wordregs_1_data
  _1WordRegS u_1wordregs_1 (
    .InputData(multiplexer_1_out), .InputAddr(BUSADDRC), .MyAddr(8'h1), .ForceInput(SP1I[0]), .nCLK(nCLK),
    .RST(BUSRST), .OutputAddrA(BUSADDRA), .OutputAddrB(BUSADDRB), .Data(n1wordregs_1_data),
    .OutputDataA(RDA), .OutputDataB(RDB));  // open: InputAddrMatch, OutputAddrAMatch, OutputAddrBMatch
  Pull_Resistor pull_resistor_20 (.node(SP5I[0]));
  _1WordRegS u_1wordregs_2 (
    .InputData(multiplexer_2_out), .InputAddr(BUSADDRC), .MyAddr(8'h5), .ForceInput(SP5I[0]), .nCLK(nCLK),
    .RST(BUSRST), .OutputAddrA(BUSADDRA), .OutputAddrB(BUSADDRB), .Data(n1wordregs_2_data),
    .OutputDataA(RDA), .OutputDataB(RDB));  // open: InputAddrMatch, OutputAddrAMatch, OutputAddrBMatch
  _1WordRegS u_1wordregs_3 (
    .InputData(BUSDATAC), .InputAddr(BUSADDRC), .MyAddr(8'h9), .ForceInput(1'b0), .nCLK(nCLK), .RST(BUSRST),
    .OutputAddrA(BUSADDRA), .OutputAddrB(BUSADDRB), .Data(n1wordregs_3_data), .OutputDataA(RDA),
    .OutputDataB(RDB));  // open: InputAddrMatch, OutputAddrAMatch, OutputAddrBMatch
  _1WordRegS u_1wordregs_4 (
    .InputData(BUSDATAC), .InputAddr(BUSADDRC), .MyAddr(8'ha), .ForceInput(1'b0), .nCLK(nCLK), .RST(BUSRST),
    .OutputAddrA(BUSADDRA), .OutputAddrB(BUSADDRB), .Data(n1wordregs_4_data), .OutputDataA(RDA),
    .OutputDataB(RDB));  // open: InputAddrMatch, OutputAddrAMatch, OutputAddrBMatch
  _1WordRegS u_1wordregs_5 (
    .InputData({PB31, PB30, PB29, PB28, PB27, PB26, PB25, PB24, PB23, PB22, PB21, PB20, PB19, PB18, PB17, PB16, PB15, PB14, PB13, PB12, PB11, PB10, PB9, PB8, PB7, PB6, PB5, PB4, PB3, PB2, PB1, PB0}),
    .InputAddr(8'h1), .MyAddr(8'hb), .ForceInput(1'b1), .nCLK(nCLK), .RST(BUSRST), .OutputAddrA(BUSADDRA),
    .OutputAddrB(BUSADDRB), .OutputDataA(RDA), .OutputDataB(RDB));  // open: InputAddrMatch, OutputAddrAMatch, OutputAddrBMatch, Data
  Counter #(.width(2), .max('h3)) counter_2 (
    .count(1'b1), .carry(counter_2_carry), .clk(and_3_out), .clr(or_2_out));  // open: load, D, Q
  and and_3 (and_3_out, nCLK, BUSRST);
  or or_3 (or_3_out, I1, I2, I3, TI, SI);
  Bit_Extender #(.in_width(32)) bit_extender_3 (.in(n1wordregs_1_data), .out(SP1O));
  Bit_Extender #(.in_width(32)) bit_extender_4 (.in(n1wordregs_2_data), .out(SP5O));
  IOCon iocon_1 (.PORT(n1wordregs_4_data[0]), .IO(PB0_2), .DDR(n1wordregs_3_data[0]));
  IOCon iocon_2 (.PORT(n1wordregs_4_data[1]), .IO(PB1_2), .DDR(n1wordregs_3_data[1]));
  IOCon iocon_3 (.PORT(n1wordregs_4_data[2]), .IO(PB2_2), .DDR(n1wordregs_3_data[2]));
  IOCon iocon_4 (.PORT(n1wordregs_4_data[3]), .IO(PB3_2), .DDR(n1wordregs_3_data[3]));
  IOCon iocon_5 (.PORT(n1wordregs_4_data[4]), .IO(PB4_2), .DDR(n1wordregs_3_data[4]));
  IOCon iocon_6 (.PORT(n1wordregs_4_data[5]), .IO(PB5_2), .DDR(n1wordregs_3_data[5]));
  IOCon iocon_7 (.PORT(n1wordregs_4_data[6]), .IO(PB6_2), .DDR(n1wordregs_3_data[6]));
  IOCon iocon_8 (.PORT(n1wordregs_4_data[7]), .IO(PB7_2), .DDR(n1wordregs_3_data[7]));
  IOCon iocon_9 (.PORT(n1wordregs_4_data[8]), .IO(PB8_2), .DDR(n1wordregs_3_data[8]));
  IOCon iocon_10 (.PORT(n1wordregs_4_data[9]), .IO(PB9_2), .DDR(n1wordregs_3_data[9]));
  IOCon iocon_11 (.PORT(n1wordregs_4_data[10]), .IO(PB10_2), .DDR(n1wordregs_3_data[10]));
  IOCon iocon_12 (.PORT(n1wordregs_4_data[11]), .IO(PB11_2), .DDR(n1wordregs_3_data[11]));
  IOCon iocon_13 (.PORT(n1wordregs_4_data[12]), .IO(PB12_2), .DDR(n1wordregs_3_data[12]));
  IOCon iocon_14 (.PORT(n1wordregs_4_data[13]), .IO(PB13_2), .DDR(n1wordregs_3_data[13]));
  IOCon iocon_15 (.PORT(n1wordregs_4_data[14]), .IO(PB14_2), .DDR(n1wordregs_3_data[14]));
  IOCon iocon_16 (.PORT(n1wordregs_4_data[15]), .IO(PB15_2), .DDR(n1wordregs_3_data[15]));
  IOCon iocon_17 (.PORT(n1wordregs_4_data[16]), .IO(PB16_2), .DDR(n1wordregs_3_data[16]));
  IOCon iocon_18 (.PORT(n1wordregs_4_data[17]), .IO(PB17_2), .DDR(n1wordregs_3_data[17]));
  IOCon iocon_19 (.PORT(n1wordregs_4_data[18]), .IO(PB18_2), .DDR(n1wordregs_3_data[18]));
  IOCon iocon_20 (.PORT(n1wordregs_4_data[19]), .IO(PB19_2), .DDR(n1wordregs_3_data[19]));
  IOCon iocon_21 (.PORT(n1wordregs_4_data[20]), .IO(PB20_2), .DDR(n1wordregs_3_data[20]));
  IOCon iocon_22 (.PORT(n1wordregs_4_data[21]), .IO(PB21_2), .DDR(n1wordregs_3_data[21]));
  IOCon iocon_23 (.PORT(n1wordregs_4_data[22]), .IO(PB22_2), .DDR(n1wordregs_3_data[22]));
  IOCon iocon_24 (.PORT(n1wordregs_4_data[23]), .IO(PB23_2), .DDR(n1wordregs_3_data[23]));
  IOCon iocon_25 (.PORT(n1wordregs_4_data[24]), .IO(PB24_2), .DDR(n1wordregs_3_data[24]));
  IOCon iocon_26 (.PORT(n1wordregs_4_data[25]), .IO(PB25_2), .DDR(n1wordregs_3_data[25]));
  IOCon iocon_27 (.PORT(n1wordregs_4_data[26]), .IO(PB26_2), .DDR(n1wordregs_3_data[26]));
  IOCon iocon_28 (.PORT(n1wordregs_4_data[27]), .IO(PB27_2), .DDR(n1wordregs_3_data[27]));
  IOCon iocon_29 (.PORT(n1wordregs_4_data[28]), .IO(PB28_2), .DDR(n1wordregs_3_data[28]));
  IOCon iocon_30 (.PORT(n1wordregs_4_data[29]), .IO(PB29_2), .DDR(n1wordregs_3_data[29]));
  IOCon iocon_31 (.PORT(n1wordregs_4_data[30]), .IO(PB30_2), .DDR(n1wordregs_3_data[30]));
  IOCon iocon_32 (.PORT(n1wordregs_4_data[31]), .IO(PB31_2), .DDR(n1wordregs_3_data[31]));
  S_R_Flip_Flop #(.trigger("high")) s_r_ff_5 (
    .S(or_2_out), .clk(1'b1), .R(counter_2_carry), .Q(BUSRST), .preset(1'b0), .reset(1'b0), .en(1'b1));  // open: Qn
  Counter #(.width(3), .max('h7), .ongoal("stay")) counter_3 (
    .load(SPSP_minus), .count(or_4_out), .Q(counter_3_q), .carry(counter_3_carry), .clk(nCLK), .clr(BUSRST));  // open: D
  or or_4 (or_4_out, SPSP_plus, SPSP_minus);
  Multiplexer #(.width(16), .disabled(0), .enable("false")) multiplexer_3 (
    .in0(adder_2_out), .in1(SPMWD), .out(multiplexer_3_out), .sel(SPMWF));
  Decoder #(.select(3), .disabled(0), .enable("false")) decoder_1 (
    .out0(decoder_1_out0), .out1(decoder_1_out1), .out2(decoder_1_out2), .out3(decoder_1_out3),
    .out4(decoder_1_out4), .out5(decoder_1_out5), .out6(decoder_1_out6), .out7(decoder_1_out7),
    .sel(counter_3_q));
  Adder #(.width(3)) adder_1 (.a(counter_3_q), .b(3'b001), .out(adder_1_out), .cin(1'b0), .cout(adder_1_cout));
  and and_4 (Stack_Overflow, adder_1_cout, SPIMWF);
  Pull_Resistor pull_resistor_21 (.node(or_3_out));
  assign or_3_out = SREGR[31] ? or_3_out : 1'bz;  // Controlled_Buffer controlled_buffer_3
  Pull_Resistor pull_resistor_22 (.node(pull_resistor_22_node));
  assign bit_extender_5_out = {{16{1'b0}}, SP2I[16:1]};  // Bit_Extender bit_extender_5
  not not_4 (not_4_out, SP2I[0]);
  assign bit_extender_6_out = {{16{1'b0}}, SP6I[16:1]};  // Bit_Extender bit_extender_6
  not not_5 (not_5_out, SP6I[0]);
  Demultiplexer #(.disabled(0), .enable("false")) demultiplexer_1 (
    .out0(Stack_Overflow), .out1(Stack_Underflow), .in(counter_3_carry), .sel(SPSP_minus));
  SPCon spcon_1 (.I({multiplexer_3_out, 1'b1}), .O(SP1I), .En(decoder_1_out0));
  SPCon spcon_2 (.I({multiplexer_3_out, 1'b1}), .O(SP2I), .En(decoder_1_out1));
  SPCon spcon_3 (.I({multiplexer_3_out, 1'b1}), .O(SP3I), .En(decoder_1_out2));
  SPCon spcon_4 (.I({multiplexer_3_out, 1'b1}), .O(SP4I), .En(decoder_1_out3));
  SPCon spcon_5 (.I({multiplexer_3_out, 1'b1}), .O(SP5I), .En(decoder_1_out4));
  SPCon spcon_6 (.I({multiplexer_3_out, 1'b1}), .O(SP6I), .En(decoder_1_out5));
  SPCon spcon_7 (.I({multiplexer_3_out, 1'b1}), .O(SP7I), .En(decoder_1_out6));
  SPCon spcon_8 (.I({multiplexer_3_out, 1'b1}), .O(SP8I), .En(decoder_1_out7));
  SPCon spcon_9 (.I({SPIMWD, SPIMWF}), .O(SP1I), .En(decoder_2_out0));
  SPCon spcon_10 (.I({SPIMWD, SPIMWF}), .O(SP2I), .En(decoder_2_out1));
  SPCon spcon_11 (.I({SPIMWD, SPIMWF}), .O(SP3I), .En(decoder_2_out2));
  SPCon spcon_12 (.I({SPIMWD, SPIMWF}), .O(SP4I), .En(decoder_2_out3));
  SPCon spcon_13 (.I({SPIMWD, SPIMWF}), .O(SP5I), .En(decoder_2_out4));
  SPCon spcon_14 (.I({SPIMWD, SPIMWF}), .O(SP6I), .En(decoder_2_out5));
  SPCon spcon_15 (.I({SPIMWD, SPIMWF}), .O(SP7I), .En(decoder_2_out6));
  SPCon spcon_16 (.I({SPIMWD, SPIMWF}), .O(SP8I), .En(decoder_2_out7));
  Decoder #(.select(3), .disabled(0), .enable("false")) decoder_2 (
    .out0(decoder_2_out0), .out1(decoder_2_out1), .out2(decoder_2_out2), .out3(decoder_2_out3),
    .out4(decoder_2_out4), .out5(decoder_2_out5), .out6(decoder_2_out6), .out7(decoder_2_out7),
    .sel(adder_1_out));
  Shift_Register #(.length(4)) shift_register_3 (
    .shift(1'b1), .in(or_3_out), .clk(nCLK), .out(shift_register_3_out), .load(1'b0), .clr(BUSRST),
    .q1(or_3_out), .q2(shift_register_3_q2));  // open: d0, q0, d1, d2, d3, q3
  buf buffer_1 (SPSP_plus, and_6_out);
  buf buffer_2 (NOCLKF, and_6_out);
  Pull_Resistor pull_resistor_23 (.node(SP2I[0]));
  Multiplexer #(.width(32), .disabled(0), .enable("false")) multiplexer_4 (
    .in0(bit_extender_5_out), .in1(BUSDATAC), .out(multiplexer_4_out), .sel(not_4_out));
  _1WordRegS u_1wordregs_6 (
    .InputData(multiplexer_4_out), .InputAddr(BUSADDRC), .MyAddr(8'h2), .ForceInput(SP2I[0]), .nCLK(nCLK),
    .RST(BUSRST), .OutputAddrA(BUSADDRA), .OutputAddrB(BUSADDRB), .Data(n1wordregs_6_data),
    .OutputDataA(RDA), .OutputDataB(RDB));  // open: InputAddrMatch, OutputAddrAMatch, OutputAddrBMatch
  // Probe on n1wordregs_6_data
  Pull_Resistor pull_resistor_24 (.node(SP6I[0]));
  Multiplexer #(.width(32), .disabled(0), .enable("false")) multiplexer_5 (
    .in0(bit_extender_6_out), .in1(BUSDATAC), .out(multiplexer_5_out), .sel(not_5_out));
  _1WordRegS u_1wordregs_7 (
    .InputData(multiplexer_5_out), .InputAddr(BUSADDRC), .MyAddr(8'h6), .ForceInput(SP6I[0]), .nCLK(nCLK),
    .RST(BUSRST), .OutputAddrA(BUSADDRA), .OutputAddrB(BUSADDRB), .Data(n1wordregs_7_data),
    .OutputDataA(RDA), .OutputDataB(RDB));  // open: InputAddrMatch, OutputAddrAMatch, OutputAddrBMatch
  and and_5 (and_5_out, I1, pull_resistor_22_node);
  assign SPIMWD = and_5_out ? 16'h2 : 16'bz;  // Controlled_Buffer controlled_buffer_4
  and and_6 (and_6_out, or_3_out, ~shift_register_3_q2);  // AND_Gate
  and and_7 (and_7_out, I2, pull_resistor_22_node);
  assign SPIMWD = and_7_out ? 16'h4 : 16'bz;  // Controlled_Buffer controlled_buffer_5
  and and_8 (and_8_out, I3, pull_resistor_22_node);
  assign SPIMWD = and_8_out ? 16'h6 : 16'bz;  // Controlled_Buffer controlled_buffer_6
  and and_9 (and_9_out, TI, pull_resistor_22_node);
  assign SPIMWD = and_9_out ? 16'h8 : 16'bz;  // Controlled_Buffer controlled_buffer_7
  and and_10 (and_10_out, SI, pull_resistor_22_node);
  assign SPIMWD = and_10_out ? 16'ha : 16'bz;  // Controlled_Buffer controlled_buffer_8
  Bit_Extender #(.in_width(32)) bit_extender_7 (.in(n1wordregs_6_data), .out(SP2O));
  Bit_Extender #(.in_width(32)) bit_extender_8 (.in(n1wordregs_7_data), .out(SP6O));
  Multiplexer #(.select(3), .width(16), .enable("false")) multiplexer_6 (
    .in0(SP1O), .in1(undriven), .in2(SP3O), .in3(SP4O), .in4(SP5O), .in5(SP6O), .in6(SP7O), .in7(SP8O),
    .out(MPA), .sel(counter_3_q));
  buf buffer_3 (SPIMWF, pull_resistor_22_node);
  assign bit_extender_9_out = {{16{1'b0}}, SP3I[16:1]};  // Bit_Extender bit_extender_9
  not not_6 (not_6_out, SP3I[0]);
  assign bit_extender_10_out = {{16{1'b0}}, SP7I[16:1]};  // Bit_Extender bit_extender_10
  not not_7 (not_7_out, SP7I[0]);
  // Probe on n1wordregs_8_data
  _1WordRegS u_1wordregs_8 (
    .InputData(BUSDATAC), .InputAddr(BUSADDRC), .MyAddr(8'h20), .ForceInput(1'b0), .nCLK(nCLK), .RST(BUSRST),
    .OutputAddrA(BUSADDRA), .OutputAddrB(BUSADDRB), .Data(n1wordregs_8_data), .OutputDataA(RDA),
    .OutputDataB(RDB));  // open: InputAddrMatch, OutputAddrAMatch, OutputAddrBMatch
  // Probe on n1wordregs_9_data
  _1WordRegS u_1wordregs_9 (
    .InputData(BUSDATAC), .InputAddr(BUSADDRC), .MyAddr(8'h24), .ForceInput(1'b0), .nCLK(nCLK), .RST(BUSRST),
    .OutputAddrA(BUSADDRA), .OutputAddrB(BUSADDRB), .Data(n1wordregs_9_data), .OutputDataA(RDA),
    .OutputDataB(RDB));  // open: InputAddrMatch, OutputAddrAMatch, OutputAddrBMatch
  // Probe on n1wordregs_10_data
  _1WordRegS u_1wordregs_10 (
    .InputData(BUSDATAC), .InputAddr(BUSADDRC), .MyAddr(8'h28), .ForceInput(1'b0), .nCLK(nCLK), .RST(BUSRST),
    .OutputAddrA(BUSADDRA), .OutputAddrB(BUSADDRB), .Data(n1wordregs_10_data), .OutputDataA(RDA),
    .OutputDataB(RDB));  // open: InputAddrMatch, OutputAddrAMatch, OutputAddrBMatch
  // Probe on n1wordregs_11_data
  _1WordRegS u_1wordregs_11 (
    .InputData(BUSDATAC), .InputAddr(BUSADDRC), .MyAddr(8'h2c), .ForceInput(1'b0), .nCLK(nCLK), .RST(BUSRST),
    .OutputAddrA(BUSADDRA), .OutputAddrB(BUSADDRB), .Data(n1wordregs_11_data), .OutputDataA(RDA),
    .OutputDataB(RDB));  // open: InputAddrMatch, OutputAddrAMatch, OutputAddrBMatch
  not not_8 (not_8_out, SREGWF);
  Multiplexer #(.width(32), .disabled(0), .enable("false")) multiplexer_7 (
    .in0(SREGW), .in1(BUSDATAC), .out(multiplexer_7_out), .sel(not_8_out));
  not not_9 (not_9_out, DNI);
  Adder #(.width(16)) adder_2 (.a({16{1'b0}}), .b(MPA), .out(adder_2_out), .cin(not_9_out), .cout(End_Of_Flash));
  Pull_Resistor pull_resistor_25 (.node(SP3I[0]));
  Multiplexer #(.width(32), .disabled(0), .enable("false")) multiplexer_8 (
    .in0(bit_extender_9_out), .in1(BUSDATAC), .out(multiplexer_8_out), .sel(not_6_out));
  _1WordRegS u_1wordregs_12 (
    .InputData(multiplexer_8_out), .InputAddr(BUSADDRC), .MyAddr(8'h3), .ForceInput(SP3I[0]), .nCLK(nCLK),
    .RST(BUSRST), .OutputAddrA(BUSADDRA), .OutputAddrB(BUSADDRB), .Data(n1wordregs_12_data),
    .OutputDataA(RDA), .OutputDataB(RDB));  // open: InputAddrMatch, OutputAddrAMatch, OutputAddrBMatch
  // Probe on n1wordregs_12_data
  Pull_Resistor pull_resistor_26 (.node(SP7I[0]));
  Multiplexer #(.width(32), .disabled(0), .enable("false")) multiplexer_9 (
    .in0(bit_extender_10_out), .in1(BUSDATAC), .out(multiplexer_9_out), .sel(not_7_out));
  _1WordRegS u_1wordregs_13 (
    .InputData(multiplexer_9_out), .InputAddr(BUSADDRC), .MyAddr(8'h7), .ForceInput(SP7I[0]), .nCLK(nCLK),
    .RST(BUSRST), .OutputAddrA(BUSADDRA), .OutputAddrB(BUSADDRB), .Data(n1wordregs_13_data),
    .OutputDataA(RDA), .OutputDataB(RDB));  // open: InputAddrMatch, OutputAddrAMatch, OutputAddrBMatch
  _1WordRegS u_1wordregs_14 (
    .InputData(multiplexer_7_out), .InputAddr(BUSADDRC), .MyAddr(8'h1f), .ForceInput(SREGWF), .nCLK(nCLK),
    .RST(BUSRST), .OutputAddrA(BUSADDRA), .OutputAddrB(BUSADDRB), .Data(SREGR), .OutputDataA(RDA),
    .OutputDataB(RDB));  // open: InputAddrMatch, OutputAddrAMatch, OutputAddrBMatch
  Shift_Register #(.length(2)) shift_register_4 (
    .shift(1'b1), .in(NOCLKF), .clk(nCLK), .load(1'b0), .clr(BUSRST), .q0(shift_register_4_q0),
    .q1(shift_register_4_q1));  // open: out, d0, d1
  buf buffer_4 (NOCLK, or_5_out);
  Bit_Extender #(.in_width(32)) bit_extender_11 (.in(n1wordregs_12_data), .out(SP3O));
  Bit_Extender #(.in_width(32)) bit_extender_12 (.in(n1wordregs_13_data), .out(SP7O));
  Pull_Resistor pull_resistor_27 (.node(SPIMWD[0]));
  Pull_Resistor pull_resistor_28 (.node(SPIMWD[1]));
  Pull_Resistor pull_resistor_29 (.node(SPIMWD[2]));
  Pull_Resistor pull_resistor_30 (.node(SPIMWD[3]));
  Pull_Resistor pull_resistor_31 (.node(SPIMWD[4]));
  Pull_Resistor pull_resistor_32 (.node(SPIMWD[5]));
  Pull_Resistor pull_resistor_33 (.node(SPIMWD[6]));
  Pull_Resistor pull_resistor_34 (.node(SPIMWD[7]));
  Pull_Resistor pull_resistor_35 (.node(SPIMWD[8]));
  Pull_Resistor pull_resistor_36 (.node(SPIMWD[9]));
  Pull_Resistor pull_resistor_37 (.node(SPIMWD[10]));
  Pull_Resistor pull_resistor_38 (.node(SPIMWD[11]));
  Pull_Resistor pull_resistor_39 (.node(SPIMWD[12]));
  Pull_Resistor pull_resistor_40 (.node(SPIMWD[13]));
  Pull_Resistor pull_resistor_41 (.node(SPIMWD[14]));
  Pull_Resistor pull_resistor_42 (.node(SPIMWD[15]));
  _1WordRegS u_1wordregs_15 (
    .InputData(BUSDATAC), .InputAddr(BUSADDRC), .MyAddr(8'h21), .ForceInput(1'b0), .nCLK(nCLK), .RST(BUSRST),
    .OutputAddrA(BUSADDRA), .OutputAddrB(BUSADDRB), .Data(n1wordregs_15_data), .OutputDataA(RDA),
    .OutputDataB(RDB));  // open: InputAddrMatch, OutputAddrAMatch, OutputAddrBMatch
  // Probe on n1wordregs_15_data
  // Probe on n1wordregs_16_data
  _1WordRegS u_1wordregs_16 (
    .InputData(BUSDATAC), .InputAddr(BUSADDRC), .MyAddr(8'h25), .ForceInput(1'b0), .nCLK(nCLK), .RST(BUSRST),
    .OutputAddrA(BUSADDRA), .OutputAddrB(BUSADDRB), .Data(n1wordregs_16_data), .OutputDataA(RDA),
    .OutputDataB(RDB));  // open: InputAddrMatch, OutputAddrAMatch, OutputAddrBMatch
  // Probe on n1wordregs_17_data
  _1WordRegS u_1wordregs_17 (
    .InputData(BUSDATAC), .InputAddr(BUSADDRC), .MyAddr(8'h29), .ForceInput(1'b0), .nCLK(nCLK), .RST(BUSRST),
    .OutputAddrA(BUSADDRA), .OutputAddrB(BUSADDRB), .Data(n1wordregs_17_data), .OutputDataA(RDA),
    .OutputDataB(RDB));  // open: InputAddrMatch, OutputAddrAMatch, OutputAddrBMatch
  // Probe on n1wordregs_18_data
  _1WordRegS u_1wordregs_18 (
    .InputData(BUSDATAC), .InputAddr(BUSADDRC), .MyAddr(8'h2d), .ForceInput(1'b0), .nCLK(nCLK), .RST(BUSRST),
    .OutputAddrA(BUSADDRA), .OutputAddrB(BUSADDRB), .Data(n1wordregs_18_data), .OutputDataA(RDA),
    .OutputDataB(RDB));  // open: InputAddrMatch, OutputAddrAMatch, OutputAddrBMatch
  Multiplexer #(.width(32), .disabled(0), .enable("false")) multiplexer_10 (
    .in0(MPD), .in1({32{1'b0}}), .out(ALU), .sel(ALUZero));
  or or_5 (or_5_out, shift_register_4_q0, shift_register_4_q1);
  buf buffer_5 (ALUZero, or_5_out);
  buf buffer_6 (DNI, or_5_out);
  assign bit_extender_13_out = {{16{1'b0}}, SP4I[16:1]};  // Bit_Extender bit_extender_13
  assign bit_extender_14_out = {{16{1'b0}}, SP8I[16:1]};  // Bit_Extender bit_extender_14
  // Probe on SPIMWD
  LED UF (.in(Stack_Underflow));
  assign IS1 = INTB[0] ? PB0 : 1'bz;  // Controlled_Buffer controlled_buffer_9
  assign IS2 = INTB[1] ? PB1 : 1'bz;  // Controlled_Buffer controlled_buffer_10
  assign IS3 = INTB[2] ? PB2 : 1'bz;  // Controlled_Buffer controlled_buffer_11
  Pull_Resistor pull_resistor_43 (.node(SP4I[0]));
  Multiplexer #(.width(32), .disabled(0), .enable("false")) multiplexer_11 (
    .in0(bit_extender_13_out), .in1(BUSDATAC), .out(multiplexer_11_out), .sel(not_10_out));
  not not_10 (not_10_out, SP4I[0]);
  // Probe on n1wordregs_19_data
  _1WordRegS u_1wordregs_19 (
    .InputData(multiplexer_11_out), .InputAddr(BUSADDRC), .MyAddr(8'h4), .ForceInput(SP4I[0]), .nCLK(nCLK),
    .RST(BUSRST), .OutputAddrA(BUSADDRA), .OutputAddrB(BUSADDRB), .Data(n1wordregs_19_data),
    .OutputDataA(RDA), .OutputDataB(RDB));  // open: InputAddrMatch, OutputAddrAMatch, OutputAddrBMatch
  Pull_Resistor pull_resistor_44 (.node(SP8I[0]));
  Multiplexer #(.width(32), .disabled(0), .enable("false")) multiplexer_12 (
    .in0(bit_extender_14_out), .in1(BUSDATAC), .out(multiplexer_12_out), .sel(not_11_out));
  not not_11 (not_11_out, SP8I[0]);
  _1WordRegS u_1wordregs_20 (
    .InputData(multiplexer_12_out), .InputAddr(BUSADDRC), .MyAddr(8'h8), .ForceInput(SP8I[0]), .nCLK(nCLK),
    .RST(BUSRST), .OutputAddrA(BUSADDRA), .OutputAddrB(BUSADDRB), .Data(n1wordregs_20_data),
    .OutputDataA(RDA), .OutputDataB(RDB));  // open: InputAddrMatch, OutputAddrAMatch, OutputAddrBMatch
  Pull_Resistor pull_resistor_45 (.node(SPMWD[0]));
  Pull_Resistor pull_resistor_46 (.node(SPMWD[1]));
  Pull_Resistor pull_resistor_47 (.node(SPMWD[2]));
  Pull_Resistor pull_resistor_48 (.node(SPMWD[3]));
  Pull_Resistor pull_resistor_49 (.node(SPMWD[4]));
  Pull_Resistor pull_resistor_50 (.node(SPMWD[5]));
  Pull_Resistor pull_resistor_51 (.node(SPMWD[6]));
  Pull_Resistor pull_resistor_52 (.node(SPMWD[7]));
  Pull_Resistor pull_resistor_53 (.node(SPMWD[8]));
  Pull_Resistor pull_resistor_54 (.node(SPMWD[9]));
  Pull_Resistor pull_resistor_55 (.node(SPMWD[10]));
  Pull_Resistor pull_resistor_56 (.node(SPMWD[11]));
  Pull_Resistor pull_resistor_57 (.node(SPMWD[12]));
  Pull_Resistor pull_resistor_58 (.node(SPMWD[13]));
  Pull_Resistor pull_resistor_59 (.node(SPMWD[14]));
  Pull_Resistor pull_resistor_60 (.node(SPMWD[15]));
  Bit_Extender #(.in_width(32)) bit_extender_15 (.in(n1wordregs_19_data), .out(SP4O));
  Bit_Extender #(.in_width(32)) bit_extender_16 (.in(n1wordregs_20_data), .out(SP8O));
  // Probe on SPMWD
  // Probe on n1wordregs_21_data
  _1WordRegS u_1wordregs_21 (
    .InputData(BUSDATAC), .InputAddr(BUSADDRC), .MyAddr(8'h22), .ForceInput(1'b0), .nCLK(nCLK), .RST(BUSRST),
    .OutputAddrA(BUSADDRA), .OutputAddrB(BUSADDRB), .Data(n1wordregs_21_data), .OutputDataA(RDA),
    .OutputDataB(RDB));  // open: InputAddrMatch, OutputAddrAMatch, OutputAddrBMatch
  // Probe on n1wordregs_22_data
  _1WordRegS u_1wordregs_22 (
    .InputData(BUSDATAC), .InputAddr(BUSADDRC), .MyAddr(8'h26), .ForceInput(1'b0), .nCLK(nCLK), .RST(BUSRST),
    .OutputAddrA(BUSADDRA), .OutputAddrB(BUSADDRB), .Data(n1wordregs_22_data), .OutputDataA(RDA),
    .OutputDataB(RDB));  // open: InputAddrMatch, OutputAddrAMatch, OutputAddrBMatch
  _1WordRegS u_1wordregs_23 (
    .InputData(BUSDATAC), .InputAddr(BUSADDRC), .MyAddr(8'h2a), .ForceInput(1'b0), .nCLK(nCLK), .RST(BUSRST),
    .OutputAddrA(BUSADDRA), .OutputAddrB(BUSADDRB), .Data(n1wordregs_23_data), .OutputDataA(RDA),
    .OutputDataB(RDB));  // open: InputAddrMatch, OutputAddrAMatch, OutputAddrBMatch
  // Probe on n1wordregs_23_data
  _1WordRegS u_1wordregs_24 (
    .InputData(BUSDATAC), .InputAddr(BUSADDRC), .MyAddr(8'h2e), .ForceInput(1'b0), .nCLK(nCLK), .RST(BUSRST),
    .OutputAddrA(BUSADDRA), .OutputAddrB(BUSADDRB), .Data(n1wordregs_24_data), .OutputDataA(RDA),
    .OutputDataB(RDB));  // open: InputAddrMatch, OutputAddrAMatch, OutputAddrBMatch
  // Probe on n1wordregs_24_data
  LED OF (.in(Stack_Overflow));
  // Probe on BUSADDRA
  Pull_Resistor pull_resistor_61 (.node(BUSADDRA[0]));
  Pull_Resistor pull_resistor_62 (.node(BUSADDRA[1]));
  Pull_Resistor pull_resistor_63 (.node(BUSADDRA[2]));
  Pull_Resistor pull_resistor_64 (.node(BUSADDRA[3]));
  Pull_Resistor pull_resistor_65 (.node(BUSADDRA[4]));
  Pull_Resistor pull_resistor_66 (.node(BUSADDRA[5]));
  Pull_Resistor pull_resistor_67 (.node(BUSADDRA[6]));
  Pull_Resistor pull_resistor_68 (.node(BUSADDRA[7]));
  _1WordRegS u_1wordregs_25 (
    .InputData(BUSDATAC), .InputAddr(BUSADDRC), .MyAddr(8'hc), .ForceInput(1'b0), .nCLK(nCLK), .RST(BUSRST),
    .OutputAddrA(BUSADDRA), .OutputAddrB(BUSADDRB), .Data(INTB), .OutputDataA(RDA), .OutputDataB(RDB));  // open: InputAddrMatch, OutputAddrAMatch, OutputAddrBMatch
  not not_12 (not_12_out, n1wordregs_26_inputaddrmatch);
  Multiplexer #(.width(32), .enable("false")) multiplexer_13 (
    .in0(adder_3_out), .in1(BUSDATAC), .out(multiplexer_13_out), .sel(n1wordregs_26_inputaddrmatch));
  or or_6 (or_6_out, shift_register_6_q1, BUSRST);
  Pull_Resistor pull_resistor_69 (.node(MDA[0]));
  Pull_Resistor pull_resistor_70 (.node(MDA[1]));
  Pull_Resistor pull_resistor_71 (.node(MDA[2]));
  Pull_Resistor pull_resistor_72 (.node(MDA[3]));
  Pull_Resistor pull_resistor_73 (.node(MDA[4]));
  Pull_Resistor pull_resistor_74 (.node(MDA[5]));
  Pull_Resistor pull_resistor_75 (.node(MDA[6]));
  Pull_Resistor pull_resistor_76 (.node(MDA[7]));
  Pull_Resistor pull_resistor_77 (.node(MDA[8]));
  Pull_Resistor pull_resistor_78 (.node(MDA[9]));
  Pull_Resistor pull_resistor_79 (.node(MDA[10]));
  Pull_Resistor pull_resistor_80 (.node(MDA[11]));
  Pull_Resistor pull_resistor_81 (.node(MDA[12]));
  Pull_Resistor pull_resistor_82 (.node(MDA[13]));
  Pull_Resistor pull_resistor_83 (.node(MDA[14]));
  Pull_Resistor pull_resistor_84 (.node(MDA[15]));
  Pull_Resistor pull_resistor_85 (.node(BUSADDRB[0]));
  Pull_Resistor pull_resistor_86 (.node(BUSADDRB[1]));
  Pull_Resistor pull_resistor_87 (.node(BUSADDRB[2]));
  Pull_Resistor pull_resistor_88 (.node(BUSADDRB[3]));
  Pull_Resistor pull_resistor_89 (.node(BUSADDRB[4]));
  Pull_Resistor pull_resistor_90 (.node(BUSADDRB[5]));
  Pull_Resistor pull_resistor_91 (.node(BUSADDRB[6]));
  Pull_Resistor pull_resistor_92 (.node(BUSADDRB[7]));
  not not_13 (not_13_out, SPIRWF);
  Multiplexer #(.width(32), .disabled(0), .enable("false")) multiplexer_14 (
    .in0({SPIRW[31:24], 1'b0, SPIRR[22], SPIRW[21:0]}), .in1(BUSDATAC), .out(multiplexer_14_out),
    .sel(not_13_out));
  Adder #(.width(32)) adder_3 (
    .a({32{1'b0}}), .b(n1wordregs_26_data), .out(adder_3_out), .cin(SREGR[3]));  // open: cout
  _1WordRegS u_1wordregs_26 (
    .InputData(multiplexer_13_out), .InputAddr(BUSADDRC), .MyAddr(8'hd),
    .InputAddrMatch(n1wordregs_26_inputaddrmatch), .ForceInput(not_12_out), .nCLK(nCLK), .RST(or_6_out),
    .OutputAddrA(BUSADDRA), .OutputAddrB(BUSADDRB), .Data(n1wordregs_26_data), .OutputDataA(RDA),
    .OutputDataB(RDB));  // open: OutputAddrAMatch, OutputAddrBMatch
  _1WordRegS u_1wordregs_27 (
    .InputData(BUSDATAC), .InputAddr(BUSADDRC), .MyAddr(8'he), .ForceInput(1'b0), .nCLK(nCLK), .RST(BUSRST),
    .OutputAddrA(BUSADDRA), .OutputAddrB(BUSADDRB), .Data(n1wordregs_27_data), .OutputDataA(RDA),
    .OutputDataB(RDB));  // open: InputAddrMatch, OutputAddrAMatch, OutputAddrBMatch
  Shift_Register #(.length(4)) shift_register_5 (
    .shift(1'b1), .in(1'b1), .clk(nCLK), .clr(BUSRST), .q2(shift_register_5_q2), .q3(shift_register_5_q3));  // open: out, load, d0, q0, d1, q1, d2, d3
  _1WordRegS u_1wordregs_28 (
    .InputData(BUSDATAC), .InputAddr(BUSADDRC), .MyAddr(8'h23), .ForceInput(1'b0), .nCLK(nCLK), .RST(BUSRST),
    .OutputAddrA(BUSADDRA), .OutputAddrB(BUSADDRB), .Data(n1wordregs_28_data), .OutputDataA(RDA),
    .OutputDataB(RDB));  // open: InputAddrMatch, OutputAddrAMatch, OutputAddrBMatch
  // Probe on n1wordregs_28_data
  // Probe on n1wordregs_29_data
  _1WordRegS u_1wordregs_29 (
    .InputData(BUSDATAC), .InputAddr(BUSADDRC), .MyAddr(8'h27), .ForceInput(1'b0), .nCLK(nCLK), .RST(BUSRST),
    .OutputAddrA(BUSADDRA), .OutputAddrB(BUSADDRB), .Data(n1wordregs_29_data), .OutputDataA(RDA),
    .OutputDataB(RDB));  // open: InputAddrMatch, OutputAddrAMatch, OutputAddrBMatch
  _1WordRegS u_1wordregs_30 (
    .InputData(BUSDATAC), .InputAddr(BUSADDRC), .MyAddr(8'h2b), .ForceInput(1'b0), .nCLK(nCLK), .RST(BUSRST),
    .OutputAddrA(BUSADDRA), .OutputAddrB(BUSADDRB), .Data(n1wordregs_30_data), .OutputDataA(RDA),
    .OutputDataB(RDB));  // open: InputAddrMatch, OutputAddrAMatch, OutputAddrBMatch
  // Probe on n1wordregs_30_data
  _1WordRegS u_1wordregs_31 (
    .InputData(BUSDATAC), .InputAddr(BUSADDRC), .MyAddr(8'h2f), .ForceInput(1'b0), .nCLK(nCLK), .RST(BUSRST),
    .OutputAddrA(BUSADDRA), .OutputAddrB(BUSADDRB), .Data(n1wordregs_31_data), .OutputDataA(RDA),
    .OutputDataB(RDB));  // open: InputAddrMatch, OutputAddrAMatch, OutputAddrBMatch
  // Probe on n1wordregs_31_data
  LED EOF (.in(End_Of_Flash));
  // Probe on BUSADDRB
  _1WordRegS u_1wordregs_32 (
    .InputData(multiplexer_14_out), .InputAddr(BUSADDRC), .MyAddr(8'hf), .ForceInput(SPIRWF), .nCLK(nCLK),
    .RST(BUSRST), .OutputAddrA(BUSADDRA), .OutputAddrB(BUSADDRB), .Data(SPIRR), .OutputDataA(RDA),
    .OutputDataB(RDB));  // open: InputAddrMatch, OutputAddrAMatch, OutputAddrBMatch
  Shift_Register #(.length(2)) shift_register_6 (
    .shift(1'b1), .in(TI), .clk(nCLK), .clr(BUSRST), .q1(shift_register_6_q1));  // open: out, load, d0, q0, d1
  Comparator #(.width(32), .mode("unsigned")) comparator_3 (
    .a(n1wordregs_26_data), .b(n1wordregs_27_data), .eq(comparator_3_eq));  // open: gt, lt
  and and_11 (TI, comparator_3_eq, SREGR[4], or_7_out);
  or or_7 (or_7_out, shift_register_5_q2, shift_register_5_q3);
  // Probe on BUSDATAC
  // Probe on BUSADDRC
  // Probe on BUSADDRC
  Pull_Resistor pull_resistor_93 (.node(BUSADDRC[0]));
  Pull_Resistor pull_resistor_94 (.node(BUSADDRC[1]));
  Pull_Resistor pull_resistor_95 (.node(BUSADDRC[2]));
  Pull_Resistor pull_resistor_96 (.node(BUSADDRC[3]));
  Pull_Resistor pull_resistor_97 (.node(BUSADDRC[4]));
  Pull_Resistor pull_resistor_98 (.node(BUSADDRC[5]));
  Pull_Resistor pull_resistor_99 (.node(BUSADDRC[6]));
  Pull_Resistor pull_resistor_100 (.node(BUSADDRC[7]));
  assign RDA = comparator_4_lt ? BUSDATAA : 32'bz;  // Controlled_Buffer controlled_buffer_12
  Comparator #(.mode("unsigned")) comparator_4 (.a(8'h1f), .b(BUSADDRA), .lt(comparator_4_lt));  // open: gt, eq
  Demultiplexer #(.select(3), .width(6), .disabled(0), .enable("false")) demultiplexer_2 (
    .out1(demultiplexer_2_out1), .out2(demultiplexer_2_out2), .out3(demultiplexer_2_out3),
    .out4(demultiplexer_2_out4), .out5(demultiplexer_2_out5), .out6(demultiplexer_2_out6),
    .out7(demultiplexer_2_out7), .in({ALU[28:24], 1'b1}), .sel(ALU[31:29]));  // open: out0
  assign RDB = comparator_5_lt ? BUSDATAB : 32'bz;  // Controlled_Buffer controlled_buffer_13
  Comparator #(.mode("unsigned")) comparator_5 (.a(8'h1f), .b(BUSADDRB), .lt(comparator_5_lt));  // open: gt, eq
  Demultiplexer #(.select(5), .disabled(0), .enable("false")) demultiplexer_3 (
    .out0(WRC), .out1(LOD), .out2(STR), .in(demultiplexer_2_out1[0]), .sel(demultiplexer_2_out1[5:1]));  // open: out3, out4, out5, out6, out7, out8, out9, out10, out11, out12, out13, out14, out15, out16, out17, out18, out19, out20, out21, out22, out23, out24, out25, out26, out27, out28, out29, out30, out31
  Demultiplexer #(.select(5), .disabled(0), .enable("false")) demultiplexer_4 (
    .out0(STI), .out1(SPSP_minus), .in(demultiplexer_2_out2[0]), .sel(demultiplexer_2_out2[5:1]));  // open: out2, out3, out4, out5, out6, out7, out8, out9, out10, out11, out12, out13, out14, out15, out16, out17, out18, out19, out20, out21, out22, out23, out24, out25, out26, out27, out28, out29, out30, out31
  not not_14 (not_14_out, shift_register_8_q0);
  Demultiplexer #(.select(5), .disabled(0), .enable("false")) demultiplexer_5 (
    .out0(ADDI), .out1(MINI), .out2(MULI), .out3(DIVI), .out4(MOD), .out5(BOR), .out6(AND), .out7(INV),
    .out16(ADDF), .out17(MINF), .out18(MULF), .out19(DIVF), .out20(SIN), .out21(COS), .out22(SQR),
    .in(demultiplexer_2_out3[0]), .sel(demultiplexer_2_out3[5:1]));  // open: out8, out9, out10, out11, out12, out13, out14, out15, out23, out24, out25, out26, out27, out28, out29, out30, out31
  Multiplexer #(.width(32), .enable("false")) multiplexer_15 (
    .in0({32{1'b0}}), .in1({ALU[15:0], {16{1'b0}}}), .out(multiplexer_15_out), .sel(CCC));
  Shift_Register #(.width(32), .length(1)) shift_register_7 (
    .shift(1'b1), .in(multiplexer_15_out), .clk(nCLK), .out(CCCD), .load(1'b0), .clr(BUSRST));  // open: d0, q0
  or or_8 (or_8_out, MDRF, MDWF);
  Register #(.width(32), .trigger("falling")) register_1 (
    .D(multiplexer_19_out), .en(not_14_out), .Q(MPD), .clk(nCLK), .clr(BUSRST));
  Register #(.width(32)) register_2 (
    .D(multiplexer_20_out), .en(shift_register_8_q0), .Q(MDRD), .clk(nCLK), .clr(BUSRST));
  not not_15 (not_15_out, MPA[15]);
  and and_12 (and_12_out, MPA[15], ~MPA[14]);  // AND_Gate
  and and_13 (and_13_out, MPA[15], MPA[14]);
  and and_14 (and_14_out, or_8_out, ~MDA[15]);  // AND_Gate
  and and_15 (and_15_out, MDA[15], ~MDA[14]);  // AND_Gate
  and and_16 (and_16_out, MDA[15], MDA[14]);
  Demultiplexer #(.select(5), .disabled(0), .enable("false")) demultiplexer_6 (
    .out0(JMC), .out1(JMR), .out2(SUC), .out3(SUR), .in(demultiplexer_2_out4[0]),
    .sel(demultiplexer_2_out4[5:1]));  // open: out4, out5, out6, out7, out8, out9, out10, out11, out12, out13, out14, out15, out16, out17, out18, out19, out20, out21, out22, out23, out24, out25, out26, out27, out28, out29, out30, out31
  // Probe on CCCD
  buf buffer_7 (WURR, LOD);
  buf buffer_8 (WURR, STR);
  and and_17 (and_17_out, not_15_out, and_14_out);
  or or_9 (or_9_out, not_15_out, and_14_out);
  or or_10 (or_10_out, and_12_out, and_15_out);
  and and_18 (and_18_out, and_12_out, and_15_out);
  or or_11 (or_11_out, and_13_out, and_16_out);
  and and_19 (and_19_out, and_13_out, and_16_out);
  assign BUSADDRC = WRC ? ALU[7:0] : 8'bz;  // Controlled_Buffer controlled_buffer_14
  assign BUSDATAC = WRC ? or_12_out : 32'bz;  // Controlled_Buffer controlled_buffer_15
  assign or_12_out = {{16{1'b0}}, ALU[23:8]} | CCCD;  // OR_Gate or_12, 32 bits wide
  buf buffer_9 (MDRF, LOD);
  assign BUSADDRC = LOD ? ALU[7:0] : 8'bz;  // Controlled_Buffer controlled_buffer_16
  assign BUSDATAC = LOD ? MDRD : 32'bz;  // Controlled_Buffer controlled_buffer_17
  buf buffer_10 (MDWF, STR);
  assign BUSADDRA = STR ? ALU[23:16] : 8'bz;  // Controlled_Buffer controlled_buffer_18
  assign RAM0W = STR ? RDA : 32'bz;  // Controlled_Buffer controlled_buffer_19
  or or_13 (or_13_out, and_17_out, and_18_out, and_19_out);
  Shift_Register #(.length(2), .trigger("falling")) shift_register_8 (
    .shift(1'b1), .in(or_13_out), .clk(nCLK), .out(shift_register_8_out), .clr(or_14_out),
    .q0(shift_register_8_q0));  // open: load, d0, d1, q1
  or or_14 (or_14_out, BUSRST, shift_register_8_out);
  Demultiplexer #(.select(5), .disabled(0), .enable("false")) demultiplexer_7 (
    .out0(IFC), .out1(IFR), .in(demultiplexer_2_out5[0]), .sel(demultiplexer_2_out5[5:1]));  // open: out2, out3, out4, out5, out6, out7, out8, out9, out10, out11, out12, out13, out14, out15, out16, out17, out18, out19, out20, out21, out22, out23, out24, out25, out26, out27, out28, out29, out30, out31
  assign MDA = LOD ? ALU[23:8] : 16'bz;  // Controlled_Buffer controlled_buffer_20
  assign MDA = STR ? ALU[15:0] : 16'bz;  // Controlled_Buffer controlled_buffer_21
  buf buffer_11 (DNI, s_r_ff_6_q);
  S_R_Flip_Flop s_r_ff_6 (.S(WURR), .clk(nCLK), .Q(s_r_ff_6_q), .reset(or_15_out), .en(1'b1));  // open: R, Qn, preset
  or or_15 (or_15_out, BUSRST, DR);
  or or_16 (DR, ~or_13_out, shift_register_8_out);  // OR_Gate
  and and_20 (and_20_out, and_12_out, ~shift_register_8_q0);  // AND_Gate
  and and_21 (and_21_out, MDRF, and_15_out);
  and and_22 (and_22_out, and_13_out, ~shift_register_8_q0);  // AND_Gate
  and and_23 (and_23_out, MDRF, and_16_out);
  not not_16 (not_16_out, or_9_out);
  or or_17 (RAM0RF, and_20_out, and_21_out);
  or or_18 (or_18_out, DR, shift_register_8_q0);
  and and_24 (RAM0WF, or_18_out, MDWF, and_15_out);
  or or_19 (RAM1RF, and_22_out, and_23_out);
  or or_20 (or_20_out, DR, shift_register_8_q0);
  and and_25 (RAM1WF, or_20_out, MDWF, and_16_out);
  Demultiplexer #(.select(5), .disabled(0), .enable("false")) demultiplexer_8 (
    .out0(FTU), .out1(FTI), .out2(UTF), .out3(ITF), .in(demultiplexer_2_out6[0]),
    .sel(demultiplexer_2_out6[5:1]));  // open: out4, out5, out6, out7, out8, out9, out10, out11, out12, out13, out14, out15, out16, out17, out18, out19, out20, out21, out22, out23, out24, out25, out26, out27, out28, out29, out30, out31
  buf buffer_12 (NOCLKF, STI);
  buf buffer_13 (SPSP_plus, STI);
  buf buffer_14 (NOCLKF, SPSP_minus);
  Multiplexer #(.width(15), .disabled(0), .enable("false")) multiplexer_16 (
    .in0(MPA[14:0]), .in1(MDA[14:0]), .out(ROMAddr), .sel(not_16_out));
  Multiplexer #(.width(14), .disabled(0), .enable("false")) multiplexer_17 (
    .in0(MPA[13:0]), .in1(MDA[13:0]), .out(RAM0Addr), .sel(or_10_out));
  Multiplexer #(.width(14), .disabled(0), .enable("false")) multiplexer_18 (
    .in0(MPA[13:0]), .in1(MDA[13:0]), .out(RAM1Addr), .sel(or_11_out));
  Multiplexer #(.select(2), .width(32), .disabled(0), .enable("false")) multiplexer_19 (
    .in0(ROMData), .in1(ROMData), .in2(RAM0R), .in3(RAM1R), .out(multiplexer_19_out), .sel(MPA[15:14]));
  Multiplexer #(.select(2), .width(32), .disabled(0), .enable("false")) multiplexer_20 (
    .in0(ROMData), .in1(ROMData), .in2(RAM0R), .in3(RAM1R), .out(multiplexer_20_out), .sel(MDA[15:14]));
  Demultiplexer #(.select(5), .disabled(0), .enable("false")) demultiplexer_9 (
    .out31(CCC), .in(demultiplexer_2_out7[0]), .sel(demultiplexer_2_out7[5:1]));  // open: out0, out1, out2, out3, out4, out5, out6, out7, out8, out9, out10, out11, out12, out13, out14, out15, out16, out17, out18, out19, out20, out21, out22, out23, out24, out25, out26, out27, out28, out29, out30
  assign BUSADDRC = ADDI ? ALU[7:0] : 8'bz;  // Controlled_Buffer controlled_buffer_22
  assign BUSDATAC = ADDI ? adder_4_out : 32'bz;  // Controlled_Buffer controlled_buffer_23
  assign BUSADDRA = ADDI ? ALU[23:16] : 8'bz;  // Controlled_Buffer controlled_buffer_24
  assign BUSADDRB = ADDI ? ALU[15:8] : 8'bz;  // Controlled_Buffer controlled_buffer_25
  assign SREGW = ADDI ? or_22_out : 32'bz;  // Controlled_Buffer controlled_buffer_26
  and and_26 (SREGWF, ADDI, adder_4_cout);
  assign BUSADDRC = MINI ? ALU[7:0] : 8'bz;  // Controlled_Buffer controlled_buffer_27
  assign BUSDATAC = MINI ? subtractor_1_out : 32'bz;  // Controlled_Buffer controlled_buffer_28
  assign BUSADDRA = MINI ? ALU[23:16] : 8'bz;  // Controlled_Buffer controlled_buffer_29
  assign BUSADDRB = MINI ? ALU[15:8] : 8'bz;  // Controlled_Buffer controlled_buffer_30
  assign SREGW = MINI ? or_23_out : 32'bz;  // Controlled_Buffer controlled_buffer_31
  and and_27 (SREGWF, MINI, subtractor_1_bout);
  assign BUSADDRC = MULI ? ALU[7:0] : 8'bz;  // Controlled_Buffer controlled_buffer_32
  assign BUSDATAC = MULI ? multiplier_1_out : 32'bz;  // Controlled_Buffer controlled_buffer_33
  assign BUSADDRA = MULI ? ALU[23:16] : 8'bz;  // Controlled_Buffer controlled_buffer_34
  assign BUSADDRB = MULI ? ALU[15:8] : 8'bz;  // Controlled_Buffer controlled_buffer_35
  assign SREGW = MULI ? or_24_out : 32'bz;  // Controlled_Buffer controlled_buffer_36
  and and_28 (SREGWF, MULI, or_25_out);
  or or_21 (or_21_out, DIVI, MOD);
  assign BUSADDRC = or_21_out ? ALU[7:0] : 8'bz;  // Controlled_Buffer controlled_buffer_37
  assign BUSADDRA = or_21_out ? ALU[23:16] : 8'bz;  // Controlled_Buffer controlled_buffer_38
  assign BUSADDRB = or_21_out ? ALU[15:8] : 8'bz;  // Controlled_Buffer controlled_buffer_39
  assign BUSDATAC = DIVI ? divider_1_out : 32'bz;  // Controlled_Buffer controlled_buffer_40
  assign BUSDATAC = MOD ? divider_1_rem : 32'bz;  // Controlled_Buffer controlled_buffer_41
  assign BUSADDRC = BOR ? ALU[7:0] : 8'bz;  // Controlled_Buffer controlled_buffer_42
  assign BUSDATAC = BOR ? or_26_out : 32'bz;  // Controlled_Buffer controlled_buffer_43
  assign BUSADDRA = BOR ? ALU[23:16] : 8'bz;  // Controlled_Buffer controlled_buffer_44
  assign BUSADDRB = BOR ? ALU[15:8] : 8'bz;  // Controlled_Buffer controlled_buffer_45
  assign BUSADDRC = AND ? ALU[7:0] : 8'bz;  // Controlled_Buffer controlled_buffer_46
  assign BUSDATAC = AND ? and_29_out : 32'bz;  // Controlled_Buffer controlled_buffer_47
  assign BUSADDRA = AND ? ALU[23:16] : 8'bz;  // Controlled_Buffer controlled_buffer_48
  assign BUSADDRB = AND ? ALU[15:8] : 8'bz;  // Controlled_Buffer controlled_buffer_49
  Adder #(.width(32)) adder_4 (.a(RDA), .b(RDB), .out(adder_4_out), .cin(1'b0), .cout(adder_4_cout));
  assign or_22_out = SREGR | 32'h1;  // OR_Gate or_22, 32 bits wide
  Subtractor #(.width(32)) subtractor_1 (
    .a(RDA), .b(RDB), .out(subtractor_1_out), .bin(1'b0), .bout(subtractor_1_bout));
  assign or_23_out = SREGR | 32'h2;  // OR_Gate or_23, 32 bits wide
  Multiplier #(.width(32)) multiplier_1 (
    .a(RDA), .b(RDB), .out(multiplier_1_out), .cin({32{1'b0}}),
    .cout({multiplier_1_cout_2, multiplier_1_cout}));
  assign or_24_out = SREGR | 32'h1;  // OR_Gate or_24, 32 bits wide
  or or_25 (or_25_out, multiplier_1_cout[0], multiplier_1_cout[1], multiplier_1_cout[2], multiplier_1_cout[3], multiplier_1_cout[4], multiplier_1_cout[5], multiplier_1_cout[6], multiplier_1_cout[7], multiplier_1_cout[8], multiplier_1_cout[9], multiplier_1_cout[10], multiplier_1_cout[11], multiplier_1_cout[12], multiplier_1_cout[13], multiplier_1_cout[14], multiplier_1_cout[15], multiplier_1_cout_2[0], multiplier_1_cout_2[1], multiplier_1_cout_2[2], multiplier_1_cout_2[3], multiplier_1_cout_2[4], multiplier_1_cout_2[5], multiplier_1_cout_2[6], multiplier_1_cout_2[7], multiplier_1_cout_2[8], multiplier_1_cout_2[9], multiplier_1_cout_2[10], multiplier_1_cout_2[11], multiplier_1_cout_2[12], multiplier_1_cout_2[13], multiplier_1_cout_2[14], multiplier_1_cout_2[15]);
  Divider #(.width(32)) divider_1 (.a(RDA), .b(RDB), .out(divider_1_out), .upper({32{1'b0}}), .rem(divider_1_rem));
  assign or_26_out = RDA | RDB;  // OR_Gate or_26, 32 bits wide
  assign and_29_out = RDA & RDB;  // AND_Gate and_29, 32 bits wide
  assign SPMWD = JMC ? ALU[23:8] : 16'bz;  // Controlled_Buffer controlled_buffer_50
  assign SPMWD = JMR ? bit_extender_17_out : 16'bz;  // Controlled_Buffer controlled_buffer_51
  assign BUSADDRA = JMR ? ALU[23:16] : 8'bz;  // Controlled_Buffer controlled_buffer_52
  assign SPIMWD = SUC ? ALU[23:8] : 16'bz;  // Controlled_Buffer controlled_buffer_53
  assign controlled_buffer_54_out = SUR ? bit_extender_18_out : 16'bz;  // Controlled_Buffer controlled_buffer_54
  assign SPIMWD = controlled_buffer_54_out;  // Buffer buffer_15, 16 bits wide
  assign BUSADDRA = SUR ? ALU[23:16] : 8'bz;  // Controlled_Buffer controlled_buffer_55
  buf buffer_16 (WURR, JMC);
  buf buffer_17 (SPMWF, JMC);
  buf buffer_18 (WURR, JMR);
  buf buffer_19 (SPMWF, JMR);
  Bit_Extender #(.in_width(32)) bit_extender_17 (.in(RDA), .out(bit_extender_17_out));
  buf buffer_20 (SPIMWF, SUC);
  buf buffer_21 (WURR, SUC);
  buf buffer_22 (WURR, SUR);
  buf buffer_23 (SPIMWF, SUR);
  Bit_Extender #(.in_width(32)) bit_extender_18 (.in(RDA), .out(bit_extender_18_out));
  Controlled_Buffer #(.width(32)) controlled_buffer_56 (.in(RDA), .en(or_27_out));  // open: out
  Controlled_Buffer #(.width(32)) controlled_buffer_57 (.in(RDB), .en(or_27_out));  // open: out
  Controlled_Buffer #(.width(32)) controlled_buffer_58 (.in(RDA), .en(SIN));  // open: out
  Controlled_Buffer #(.width(32)) controlled_buffer_59 (.in(RDA), .en(COS));  // open: out
  Controlled_Buffer #(.width(32)) controlled_buffer_60 (.in(RDA), .en(SQR));  // open: out
  assign BUSADDRC = INV ? ALU[7:0] : 8'bz;  // Controlled_Buffer controlled_buffer_61
  assign BUSDATAC = INV ? not_17_out : 32'bz;  // Controlled_Buffer controlled_buffer_62
  assign not_17_out = ~RDA;  // NOT_Gate not_17, 32 bits wide
  assign BUSADDRA = INV ? ALU[23:16] : 8'bz;  // Controlled_Buffer controlled_buffer_63
  or or_27 (or_27_out, ADDF, MINF, DIVF, MULF);
  assign BUSADDRC = or_27_out ? ALU[7:0] : 8'bz;  // Controlled_Buffer controlled_buffer_64
  // Calculator calculator_1: pin names not known; wires that end beside it: calculator_1_p1, calculator_1_p2, calculator_1_p3, calculator_1_p4, calculator_1_p5
  assign BUSADDRA = or_27_out ? ALU[23:16] : 8'bz;  // Controlled_Buffer controlled_buffer_65
  assign BUSADDRB = or_27_out ? ALU[15:8] : 8'bz;  // Controlled_Buffer controlled_buffer_66
  assign BUSDATAC = ADDF ? calculator_1_p2 : 32'bz;  // Controlled_Buffer controlled_buffer_67
  assign BUSDATAC = MINF ? calculator_1_p3 : 32'bz;  // Controlled_Buffer controlled_buffer_68
  assign BUSDATAC = DIVF ? calculator_1_p5 : 32'bz;  // Controlled_Buffer controlled_buffer_69
  assign BUSDATAC = MULF ? calculator_1_p4 : 32'bz;  // Controlled_Buffer controlled_buffer_70
  assign SREGW = DIVF ? or_28_out : 32'bz;  // Controlled_Buffer controlled_buffer_71
  assign or_28_out = SREGR | 32'h4;  // OR_Gate or_28, 32 bits wide
  and and_30 (SREGWF, DIVF, calculator_1_p1);
  assign BUSADDRC = SIN ? ALU[7:0] : 8'bz;  // Controlled_Buffer controlled_buffer_72
  assign BUSDATAC = SIN ? sin_1_p1 : 32'bz;  // Controlled_Buffer controlled_buffer_73
  // sin sin_1: pin names not known; wires that end beside it: sin_1_p1
  assign BUSADDRA = SIN ? ALU[23:16] : 8'bz;  // Controlled_Buffer controlled_buffer_74
  assign BUSADDRC = COS ? ALU[7:0] : 8'bz;  // Controlled_Buffer controlled_buffer_75
  assign BUSDATAC = COS ? cos_1_p1 : 32'bz;  // Controlled_Buffer controlled_buffer_76
  // cos cos_1: pin names not known; wires that end beside it: cos_1_p1
  assign BUSADDRA = COS ? ALU[23:16] : 8'bz;  // Controlled_Buffer controlled_buffer_77
  assign BUSADDRC = SQR ? ALU[7:0] : 8'bz;  // Controlled_Buffer controlled_buffer_78
  assign BUSDATAC = SQR ? sqrt_1_p1 : 32'bz;  // Controlled_Buffer controlled_buffer_79
  // sqrt sqrt_1: pin names not known; wires that end beside it: sqrt_1_p1
  assign BUSADDRA = SQR ? ALU[23:16] : 8'bz;  // Controlled_Buffer controlled_buffer_80
  assign BUSADDRA = IFC ? ALU[23:16] : 8'bz;  // Controlled_Buffer controlled_buffer_81
  and and_31 (and_31_out, IFC, not_18_out);
  buf buffer_24 (NOCLKF, and_31_out);
  buf buffer_25 (SPMWF, and_31_out);
  assign SPMWD = and_31_out ? ALU[15:0] : 16'bz;  // Controlled_Buffer controlled_buffer_82
  assign BUSADDRA = IFR ? ALU[23:16] : 8'bz;  // Controlled_Buffer controlled_buffer_83
  assign BUSADDRB = IFR ? ALU[15:8] : 8'bz;  // Controlled_Buffer controlled_buffer_84
  and and_32 (and_32_out, IFR, not_19_out);
  buf buffer_26 (NOCLKF, and_32_out);
  buf buffer_27 (SPMWF, and_32_out);
  assign SPMWD = and_32_out ? bit_extender_19_out : 16'bz;  // Controlled_Buffer controlled_buffer_85
  not not_18 (not_18_out, comparator_6_eq);
  Comparator #(.width(32), .mode("unsigned")) comparator_6 (
    .a({32{1'b0}}), .b(RDA), .eq(comparator_6_eq));  // open: gt, lt
  Comparator #(.width(32), .mode("unsigned")) comparator_7 (
    .a({32{1'b0}}), .b(RDA), .eq(comparator_7_eq));  // open: gt, lt
  not not_19 (not_19_out, comparator_7_eq);
  Bit_Extender #(.in_width(32)) bit_extender_19 (.in(RDB), .out(bit_extender_19_out));
  assign BUSADDRC = FTU ? ALU[7:0] : 8'bz;  // Controlled_Buffer controlled_buffer_86
  assign BUSDATAC = FTU ? n32bitfptouint_1_p2 : 32'bz;  // Controlled_Buffer controlled_buffer_87
  // _32BitFPtoUInt 32bitfptouint_1: pin names not known; wires that end beside it: RDA, n32bitfptouint_1_p2
  assign BUSADDRA = FTU ? ALU[23:16] : 8'bz;  // Controlled_Buffer controlled_buffer_88
  assign BUSADDRC = FTI ? ALU[7:0] : 8'bz;  // Controlled_Buffer controlled_buffer_89
  assign BUSDATAC = FTI ? n32bitfptoint_1_p2 : 32'bz;  // Controlled_Buffer controlled_buffer_90
  // _32BitFPtoInt 32bitfptoint_1: pin names not known; wires that end beside it: RDA, n32bitfptoint_1_p2
  assign BUSADDRA = FTI ? ALU[23:16] : 8'bz;  // Controlled_Buffer controlled_buffer_91
  assign BUSADDRC = UTF ? ALU[7:0] : 8'bz;  // Controlled_Buffer controlled_buffer_92
  assign BUSDATAC = UTF ? uintto32bitfp_1_p2 : 32'bz;  // Controlled_Buffer controlled_buffer_93
  assign BUSADDRA = UTF ? ALU[23:16] : 8'bz;  // Controlled_Buffer controlled_buffer_94
  assign BUSADDRC = ITF ? ALU[7:0] : 8'bz;  // Controlled_Buffer controlled_buffer_95
  assign BUSDATAC = ITF ? intto32bitfp_1_p2 : 32'bz;  // Controlled_Buffer controlled_buffer_96
  assign BUSADDRA = ITF ? ALU[23:16] : 8'bz;  // Controlled_Buffer controlled_buffer_97
  // UIntto32bitFP uintto32bitfp_1: pin names not known; wires that end beside it: RDA, uintto32bitfp_1_p2
  // Intto32BitFP intto32bitfp_1: pin names not known; wires that end beside it: RDA, intto32bitfp_1_p2

  assign BUSCLK = nCLK;
  assign RAM1W = RAM0W;
  // also tied to GND on the sheet: SPIRWF

  // Other names for the same wires on the sheet: CB3[7:0] = ALU[23:16]; CB1[7:0] = ALU[7:0]; CB2[7:0] = ALU[15:8];
  //   MDWD[31:0] = RAM0W;
  //   PBB[31:0] = {PB31, PB30, PB29, PB28, PB27, PB26, PB25, PB24, PB23, PB22, PB21, PB20, PB19, PB18, PB17, PB16, PB15, PB14, PB13, PB12, PB11, PB10, PB9, PB8, PB7, PB6, PB5, PB4, PB3, PB2, PB1, PB0};
  //   RAA[7:0] = BUSADDRA; RAB[7:0] = BUSADDRB; REGW[31:0] = BUSDATAC; REGWAddr[7:0] = BUSADDRC; RST_t = BUSRST;
  //   SPIRW[22] = SPIRR[22]; STD = SPSP_minus

  // Notes on the sheet:
  //   DDRB
  //   PORTB
  //   PINB
  //   by Penta0308
  //   PentaXMega2 Core
  //   SP1
  //   SP1
  //   and_4 drives only 1 and floats otherwise
  //   buffer_1 drives only 1 and floats otherwise
  //   buffer_2 drives only 1 and floats otherwise
  //   SP1
  //   SP1
  //   STACK POINTERS
  //   buffer_3 drives only 1 and floats otherwise
  //   SP1
  //   SP1
  //   SP1
  //   buffer_4 drives only 1 and floats otherwise
  //   buffer_5 drives only 1 and floats otherwise
  //   buffer_6 drives only 1 and floats otherwise
  //   SP1
  //   SP1
  //   INTB
  //   SPIR
  //   ROM
  //   RAM0
  //   RAM1
  //   ROM
  //   RAM0
  //   RAM1
  //   buffer_7 drives only 1 and floats otherwise
  //   buffer_8 drives only 1 and floats otherwise
  //   buffer_11 drives only 1 and floats otherwise
  //   buffer_12 drives only 1 and floats otherwise
  //   buffer_13 drives only 1 and floats otherwise
  //   buffer_14 drives only 1 and floats otherwise
  //   buffer_15 drives only 1 and floats otherwise
  //   buffer_16 drives only 1 and floats otherwise
  //   buffer_17 drives only 1 and floats otherwise
  //   buffer_18 drives only 1 and floats otherwise
  //   buffer_19 drives only 1 and floats otherwise
  //   buffer_20 drives only 1 and floats otherwise
  //   buffer_21 drives only 1 and floats otherwise
  //   buffer_22 drives only 1 and floats otherwise
  //   buffer_23 drives only 1 and floats otherwise
  //   buffer_24 drives only 1 and floats otherwise
  //   buffer_25 drives only 1 and floats otherwise
  //   buffer_26 drives only 1 and floats otherwise
  //   buffer_27 drives only 1 and floats otherwise
endmodule

module main (
);

  wire button_1_out, clock_1_out, clock_2_out, clock_3_out, leddimmingpwmmodule_1_a, leddimmingpwmmodule_1_b,
       leddimmingpwmmodule_1_c, leddimmingpwmmodule_1_d, not_1_out, pentacortexa2core_1_busclk,
       pentacortexa2core_1_busrst, pentacortexa2core_1_pb0_2, pentacortexa2core_1_pb1_2,
       pentacortexa2core_1_pb2_2, pentacortexa2core_1_pb3_2, pentacortexa2core_1_pb4_2,
       pentacortexa2core_1_pb5_2, pentacortexa2core_1_pb6_2, pentacortexa2core_1_pb7_2,
       pentacortexa2core_1_pb8_2, pentacortexa2core_1_pb9_2, pentacortexa2core_1_pb10_2,
       pentacortexa2core_1_pb11_2, pentacortexa2core_1_pb12_2, pentacortexa2core_1_pb13_2,
       pentacortexa2core_1_pb14_2, pentacortexa2core_1_pb15_2, pentacortexa2core_1_pb16_2,
       pentacortexa2core_1_pb17_2, pentacortexa2core_1_pb18_2, pentacortexa2core_1_pb19_2,
       pentacortexa2core_1_pb20_2, pentacortexa2core_1_pb21_2, pentacortexa2core_1_pb22_2,
       pentacortexa2core_1_pb23_2, pentacortexa2core_1_pb24_2, pentacortexa2core_1_pb25_2,
       pentacortexa2core_1_pb26_2, pentacortexa2core_1_pb27_2, pentacortexa2core_1_pb28_2,
       pentacortexa2core_1_pb29_2, pentacortexa2core_1_pb30_2, pentacortexa2core_1_pb31_2,
       pentacortexa2core_1_ram0rf, pentacortexa2core_1_ram0wf, pentacortexa2core_1_ram1rf,
       pentacortexa2core_1_ram1wf;
  wire [7:0] pentacortexa2core_1_busaddra, pentacortexa2core_1_busaddrb, pentacortexa2core_1_busaddrc;
  wire [13:0] pentacortexa2core_1_ram0addr, pentacortexa2core_1_ram1addr;
  wire [14:0] pentacortexa2core_1_romaddr;
  wire [31:0] pentacortexa2core_1_ram0w, pentacortexa2core_1_ram1w, pentaxmegaextensioncard_1_bdc_2,
       ram_1_data, ram_2_data, rom_1_data, undriven, undriven_2;

  Clock #(.highDuration(40), .lowDuration(60)) clock_1 (.out(clock_1_out));
  LED led_1 (.in(leddimmingpwmmodule_1_d));
  LED led_2 (.in(leddimmingpwmmodule_1_a));
  LED led_3 (.in(leddimmingpwmmodule_1_c));
  LEDDimmingPWMModule leddimmingpwmmodule_1 (
    .PWMIN(clock_1_out), .CLK(clock_2_out), .D(leddimmingpwmmodule_1_d), .C(leddimmingpwmmodule_1_c),
    .B(leddimmingpwmmodule_1_b), .A(leddimmingpwmmodule_1_a));
  LED led_4 (.in(leddimmingpwmmodule_1_b));
  Clock clock_2 (.out(clock_2_out));
  PentaXMegaExtensionCard pentaxmegaextensioncard_1 (
    .BAA(pentacortexa2core_1_busaddra), .BAB(pentacortexa2core_1_busaddrb),
    .BAC(pentacortexa2core_1_busaddrc), .BDA(undriven), .BDB(undriven_2),
    .BDC_2(pentaxmegaextensioncard_1_bdc_2), .BUSRST(pentacortexa2core_1_busrst),
    .CLK(pentacortexa2core_1_busclk));  // open: BAA_2, BAB_2, BAC_2, BDA_2, BDB_2, BDC, BUSRST_2, CLK_2
  PentaCortexA2Core pentacortexa2core_1 (
    .RST(button_1_out), .nCLK(clock_3_out), .PB1(pentacortexa2core_1_pb1_2), .PB3(pentacortexa2core_1_pb3_2),
    .PB5(pentacortexa2core_1_pb5_2), .PB7(pentacortexa2core_1_pb7_2), .PB9(pentacortexa2core_1_pb9_2),
    .PB10(pentacortexa2core_1_pb11_2), .PB11(pentacortexa2core_1_pb13_2), .PB12(pentacortexa2core_1_pb15_2),
    .PB13(pentacortexa2core_1_pb17_2), .PB14(pentacortexa2core_1_pb19_2), .PB15(pentacortexa2core_1_pb21_2),
    .PB16(pentacortexa2core_1_pb23_2), .PB17(pentacortexa2core_1_pb25_2), .PB18(pentacortexa2core_1_pb27_2),
    .PB19(pentacortexa2core_1_pb29_2), .PB20(pentacortexa2core_1_pb31_2), .PB21(pentacortexa2core_1_pb2_2),
    .PB22(pentacortexa2core_1_pb4_2), .PB23(pentacortexa2core_1_pb6_2), .PB24(pentacortexa2core_1_pb8_2),
    .PB25(pentacortexa2core_1_pb10_2), .PB26(pentacortexa2core_1_pb12_2), .PB27(pentacortexa2core_1_pb14_2),
    .PB28(pentacortexa2core_1_pb16_2), .PB29(pentacortexa2core_1_pb18_2), .PB30(pentacortexa2core_1_pb20_2),
    .PB31(pentacortexa2core_1_pb22_2), .BUSADDRA(pentacortexa2core_1_busaddra),
    .BUSADDRB(pentacortexa2core_1_busaddrb), .BUSADDRC(pentacortexa2core_1_busaddrc), .BUSDATAA(undriven),
    .BUSDATAB(undriven_2), .BUSDATAC(pentaxmegaextensioncard_1_bdc_2), .PB1_2(pentacortexa2core_1_pb1_2),
    .PB3_2(pentacortexa2core_1_pb3_2), .PB5_2(pentacortexa2core_1_pb5_2), .PB7_2(pentacortexa2core_1_pb7_2),
    .PB9_2(pentacortexa2core_1_pb9_2), .PB11_2(pentacortexa2core_1_pb11_2),
    .PB13_2(pentacortexa2core_1_pb13_2), .PB15_2(pentacortexa2core_1_pb15_2),
    .PB17_2(pentacortexa2core_1_pb17_2), .PB19_2(pentacortexa2core_1_pb19_2),
    .PB21_2(pentacortexa2core_1_pb21_2), .PB23_2(pentacortexa2core_1_pb23_2),
    .PB25_2(pentacortexa2core_1_pb25_2), .PB27_2(pentacortexa2core_1_pb27_2),
    .PB29_2(pentacortexa2core_1_pb29_2), .PB31_2(pentacortexa2core_1_pb31_2),
    .PB0_2(pentacortexa2core_1_pb0_2), .PB2_2(pentacortexa2core_1_pb2_2), .PB4_2(pentacortexa2core_1_pb4_2),
    .PB6_2(pentacortexa2core_1_pb6_2), .PB8_2(pentacortexa2core_1_pb8_2),
    .PB10_2(pentacortexa2core_1_pb10_2), .PB12_2(pentacortexa2core_1_pb12_2),
    .PB14_2(pentacortexa2core_1_pb14_2), .PB16_2(pentacortexa2core_1_pb16_2),
    .PB18_2(pentacortexa2core_1_pb18_2), .PB20_2(pentacortexa2core_1_pb20_2),
    .PB22_2(pentacortexa2core_1_pb22_2), .PB24_2(pentacortexa2core_1_pb24_2),
    .PB26_2(pentacortexa2core_1_pb26_2), .PB28_2(pentacortexa2core_1_pb28_2),
    .PB30_2(pentacortexa2core_1_pb30_2), .PB0(pentacortexa2core_1_pb0_2), .PB2(pentacortexa2core_1_pb24_2),
    .PB4(pentacortexa2core_1_pb26_2), .PB6(pentacortexa2core_1_pb28_2), .PB8(pentacortexa2core_1_pb30_2),
    .BUSRST(pentacortexa2core_1_busrst), .BUSCLK(pentacortexa2core_1_busclk),
    .ROMAddr(pentacortexa2core_1_romaddr), .RAM0Addr(pentacortexa2core_1_ram0addr),
    .RAM1Addr(pentacortexa2core_1_ram1addr), .ROMData(rom_1_data), .RAM0R(ram_1_data),
    .RAM0W(pentacortexa2core_1_ram0w), .RAM1R(ram_2_data), .RAM1W(pentacortexa2core_1_ram1w),
    .RAM0RF(pentacortexa2core_1_ram0rf), .RAM0WF(pentacortexa2core_1_ram0wf),
    .RAM1RF(pentacortexa2core_1_ram1rf), .RAM1WF(pentacortexa2core_1_ram1wf));  // open: MOSI, MISO, SCK
  Button button_1 (.out(button_1_out));
  Clock clock_3 (.out(clock_3_out));
  RAM #(.addrWidth(14), .dataWidth(32), .bus("separate")) ram_1 (
    .addr(pentacortexa2core_1_ram0addr), .din(pentacortexa2core_1_ram0w), .data(ram_1_data),
    .str(pentacortexa2core_1_ram0wf), .sel(1'b1), .clk(not_1_out), .ld(pentacortexa2core_1_ram0rf),
    .clr(button_1_out));
  RAM #(.addrWidth(14), .dataWidth(32), .bus("separate")) ram_2 (
    .addr(pentacortexa2core_1_ram1addr), .din(pentacortexa2core_1_ram1w), .data(ram_2_data),
    .str(pentacortexa2core_1_ram1wf), .sel(1'b1), .clk(not_1_out), .ld(pentacortexa2core_1_ram1rf),
    .clr(button_1_out));
  ROM #(.addrWidth(15), .dataWidth(32)) rom_1 (.addr(pentacortexa2core_1_romaddr), .data(rom_1_data), .sel(1'b1));
  not not_1 (not_1_out, clock_3_out);

  // Notes on the sheet:
  //   contents of rom_1 (hex, n*v repeats v):
  //   0 80000c00 0 41000000 0 41000000 0 41000000 0 41000000 0 41000000 0 80000c00
endmodule

module _1WordRegS (
  input  [31:0] InputData,
  input  ForceInput,
  input  [7:0] InputAddr,
  input  [7:0] MyAddr,
  input  nCLK,
  input  RST,
  input  [7:0] OutputAddrA,
  input  [7:0] OutputAddrB,
  output InputAddrMatch,
  output OutputAddrAMatch,
  output OutputAddrBMatch,
  output [31:0] Data,
  output [31:0] OutputDataA,
  output [31:0] OutputDataB
);

  wire or_1_out;

  Pull_Resistor pull_resistor_1 (.node(InputAddrMatch));
  Comparator #(.mode("unsigned")) comparator_1 (.a(InputAddr), .b(MyAddr), .eq(InputAddrMatch));  // open: gt, lt
  or or_1 (or_1_out, ForceInput, InputAddrMatch);
  Comparator #(.mode("unsigned")) comparator_2 (.a(MyAddr), .b(OutputAddrA), .eq(OutputAddrAMatch));  // open: gt, lt
  Pull_Resistor pull_resistor_2 (.node(nCLK));
  Comparator #(.mode("unsigned")) comparator_3 (.a(MyAddr), .b(OutputAddrB), .eq(OutputAddrBMatch));  // open: gt, lt
  Pull_Resistor pull_resistor_3 (.node(ForceInput));
  Pull_Resistor pull_resistor_4 (.node(OutputAddrAMatch));
  Register #(.width(32)) register_1 (.D(InputData), .en(or_1_out), .Q(Data), .clk(nCLK), .clr(RST));
  Pull_Resistor pull_resistor_5 (.node(RST));
  assign OutputDataA = OutputAddrAMatch ? Data : 32'bz;  // Controlled_Buffer controlled_buffer_1
  assign OutputDataB = OutputAddrBMatch ? Data : 32'bz;  // Controlled_Buffer controlled_buffer_2
  Pull_Resistor pull_resistor_6 (.node(OutputAddrBMatch));

  // Notes on the sheet:
  //   OutputAddrA: pull=down
  //   RST: pull=down
  //   InputData: pull=down
  //   OutputAddrB: pull=down
  //   InputAddr: pull=down
  //   MyAddr: pull=down
endmodule

module IOCon (
  input  DDR,
  input  PORT,
  output IO
);

  assign IO = DDR ? PORT : 1'bz;  // Controlled_Buffer controlled_buffer_1

  // Notes on the sheet:
  //   PORT: pull=down
  //   DDR: pull=down
endmodule

module SPCon (
  input  En,
  input  [16:0] I,
  output [16:0] O
);

  assign O = En ? I : 17'bz;  // Controlled_Buffer controlled_buffer_1

  // Notes on the sheet:
  //   En: pull=down
  //   I: pull=down
endmodule

module PentaXMegaExtensionCard (
  input  [31:0] BDC,
  input  [7:0] BAA,
  input  [7:0] BAB,
  input  [7:0] BAC,
  input  [31:0] BDA,
  input  [31:0] BDB,
  input  BUSRST,
  input  CLK,
  output [7:0] BAA_2,
  output [7:0] BAB_2,
  output [7:0] BAC_2,
  output [31:0] BDA_2,
  output [31:0] BDB_2,
  output BUSRST_2,
  output CLK_2,
  output [31:0] BDC_2
);


  assign BAA_2 = BAA;
  assign BAB_2 = BAB;
  assign BAC_2 = BAC;
  assign BDA_2 = BDA;
  assign BDB_2 = BDB;
  assign BDC_2 = BDC;
  assign BUSRST_2 = BUSRST;
  assign CLK_2 = CLK;
endmodule

module LEDDimmingPWMModule (
  input  PWMIN,
  input  CLK,
  output D,
  output C,
  output B,
  output A
);

  wire [4:0] bitadder_1_out;
  wire [30:0] shift_register_1_q30;

  Shift_Register #(.length(31)) shift_register_1 (
    .shift(1'b1), .in(PWMIN), .clk(CLK), .load(1'b0), .clr(1'b0), .q0(shift_register_1_q30[30]),
    .q1(shift_register_1_q30[29]), .q2(shift_register_1_q30[28]), .q3(shift_register_1_q30[27]),
    .q4(shift_register_1_q30[26]), .q5(shift_register_1_q30[25]), .q6(shift_register_1_q30[24]),
    .q7(shift_register_1_q30[23]), .q8(shift_register_1_q30[22]), .q9(shift_register_1_q30[21]),
    .q10(shift_register_1_q30[20]), .q11(shift_register_1_q30[19]), .q12(shift_register_1_q30[18]),
    .q13(shift_register_1_q30[17]), .q14(shift_register_1_q30[16]), .q15(shift_register_1_q30[15]),
    .q16(shift_register_1_q30[14]), .q17(shift_register_1_q30[13]), .q18(shift_register_1_q30[12]),
    .q19(shift_register_1_q30[11]), .q20(shift_register_1_q30[10]), .q21(shift_register_1_q30[9]),
    .q22(shift_register_1_q30[8]), .q23(shift_register_1_q30[7]), .q24(shift_register_1_q30[6]),
    .q25(shift_register_1_q30[5]), .q26(shift_register_1_q30[4]), .q27(shift_register_1_q30[3]),
    .q28(shift_register_1_q30[2]), .q29(shift_register_1_q30[1]), .q30(shift_register_1_q30[0]));  // open: out, d0, d1, d2, d3, d4, d5, d6, d7, d8, d9, d10, d11, d12, d13, d14, d15, d16, d17, d18, d19, d20, d21, d22, d23, d24, d25, d26, d27, d28, d29, d30
  BitAdder #(.width(31)) bitadder_1 (.in0(shift_register_1_q30), .out(bitadder_1_out));
  Comparator #(.width(5), .mode("unsigned")) comparator_1 (.a(5'b11001), .b(bitadder_1_out), .lt(D));  // open: gt, eq
  Comparator #(.width(5), .mode("unsigned")) comparator_2 (.a(5'b10011), .b(bitadder_1_out), .lt(C));  // open: gt, eq
  Comparator #(.width(5), .mode("unsigned")) comparator_3 (.a(5'b01100), .b(bitadder_1_out), .lt(B));  // open: gt, eq
  Comparator #(.width(5), .mode("unsigned")) comparator_4 (.a(5'b00110), .b(bitadder_1_out), .lt(A));  // open: gt, eq
endmodule
