// Logisim project Test.circ as structural Verilog: 1 circuit, main circuit main
module main (
  input  [15:0] in_1,
  input  [15:0] in_2,
  input  [15:0] in_3,
  input  [15:0] in_4,
  output [15:0] out_5,
  output [15:0] out_6
);

  wire [15:0] and_1_out, E_2_out, E_out, nor_1_out, nor_2_out, or_3_out, or_4_out, R_out;

  assign nor_1_out = ~(in_1 | in_2);  // NOR_Gate nor_1, 16 bits wide
  assign nor_2_out = ~(in_3 | in_4);  // NOR_Gate nor_2, 16 bits wide
  assign and_1_out = nor_1_out & nor_2_out;  // AND_Gate and_1, 16 bits wide
  assign R_out = in_1 & in_3;  // AND_Gate R, 16 bits wide
  assign E_out = in_1 & in_3;  // AND_Gate E, 16 bits wide
  assign E_2_out = in_2 & in_4;  // AND_Gate E_2, 16 bits wide
  assign out_5 = R_out | or_4_out;  // OR_Gate or_1, 16 bits wide
  assign out_6 = or_4_out | or_4_out;  // OR_Gate or_2, 16 bits wide
  assign or_3_out = E_out | E_2_out;  // OR_Gate or_3, 16 bits wide
  assign or_4_out = or_3_out | and_1_out;  // OR_Gate or_4, 16 bits wide
endmodule
