// Logisim project firstlast-updown.circ as structural Verilog: 3 circuits, main circuit main
module main (
);

  \먼저가_위  \u_먼저가_위_1  ();  // open: 먼저, 나중에
  \먼저가_아래  \u_먼저가_아래_1  ();  // open: 먼저, 나중에
endmodule

module \먼저가_위  (
  input  \먼저 ,
  input  \나중에 
);
endmodule

module \먼저가_아래  (
  input  \먼저 ,
  input  \나중에 
);
endmodule
